# Fritzing sketch HC-05_Setup_Breadboard (saved by Fritzing 0.9.5d)
breadboards: 1

parts:
  Part1 = Arduino Nano (Rev3.0)
  Part2 = Bluetooth HC-05 Macho
  R2 = Resistor [tolerance=±5% resistance=1k package=THT]
  R3 = Resistor [tolerance=±5% resistance=2k package=THT]

nets:
  N1: Part1.D1/TX, R2.Pin_0
  N2: Part1.D0/RX, Part2.TXD
  GND: Part1.GND, Part2.GND, R3.Pin_0
  5V: Part1.5V, Part2.VCC
  N3: Part2.RXD, R2.Pin_1, R3.Pin_1
