# Fritzing sketch door_module_schematics (saved by Fritzing 0.9.5d)
breadboards: 1

parts:
  Part1 = Arduino Uno (Rev3)
  Part2 = Bluetooth HC-05 Macho
  LED1 = RGB LED (com. cathode, rbg) [package="5 mm [THT]"]
  R1 = Resistor [tolerance=±5% resistance=220 package="0805 [SMD]"]
  R2 = Resistor [tolerance=±5% resistance=220 package="0805 [SMD]"]
  R3 = Resistor [tolerance=±5% resistance=220 package="0805 [SMD]"]
  R4 = Resistor [tolerance=±5% resistance=1000 package="0805 [SMD]"]
  R5 = Resistor [tolerance=±5% resistance=2000 package="0805 [SMD]"]
  S1 = Reed switch [package=THT]
  R6 = Resistor [tolerance=±5% resistance=220 package="0805 [SMD]"]

nets:
  N1: Part1.D9_PWM, R1.Pin_0
  N2: Part1.D10_PWM/SS, Part2.TXD
  N3: Part1.D11_PWM/MOSI, R4.Pin_0
  N4: Part1.D4, S1.pin_2, R6.Pin_1
  N5: Part1.D5_PWM, R2.Pin_0
  N6: Part1.D6_PWM, R3.Pin_0
  5V: Part1.5V, Part2.VCC, S1.pin_1
  GND: Part1.GND, Part2.GND, LED1.common_cathode, R5.Pin_0, R6.Pin_0
  N7: Part2.RXD, R4.Pin_1, R5.Pin_1
  N8: LED1.red_anode, R1.Pin_1
  N9: LED1.blue_anode, R2.Pin_1
  N10: LED1.green_anode, R3.Pin_1

notes:
  Reed Switch
